# Fritzing sketch Schéma montage (saved by Fritzing 0.9.3b)
breadboards: 1

parts:
  Q1 = Basic FET P-Channel [package="TO220 [THT]"]
  RHT1 = Humidity and Temperature Sensor RHT03
  R1 = Resistor [tolerance=±5% resistance=10k package="2512 [SMD]"]
  Composant1 = Arduino Uno (Rev3)
  R2 = Resistor [tolerance=±5% resistance=10k package="2512 [SMD]"]
  J1 = Peltier Element

nets:
  N1: Q1.gate, Composant1.D3_PWM, R2.Pin_1
  N2: Q1.drain, J1.pin1
  N3: Q1.source, RHT1.GND_2, Composant1.GND, R2.Pin_0
  VCC: RHT1.Vcc, Composant1.5V
  N4: RHT1.Data-signal, R1.Pin_1, Composant1.D2
  N5: Composant1.VIN, J1.pin2
